# Fritzing sketch arduino_birthday_cake_breadboard (saved by Fritzing 0.9.3b)
breadboards: 1

parts:
  lel = Arduino Uno (Rev3)
  J1 = Piezo Speaker
  R1 = Resistor [tolerance=±5% resistance=1M package="0603 [SMD]"]
  LED1 = LED - 3mm [color="Red (633nm)" package="3 mm [THT]"]
  LED2 = LED - 3mm [color="Red (633nm)" package="3 mm [THT]"]
  R2 = Resistor [tolerance=±5% resistance=220 package="0603 [SMD]"]
  R3 = Resistor [tolerance=±5% resistance=220 package="0603 [SMD]"]

nets:
  N1: lel.A0, J1.pin1, R1.Pin_1
  N2: lel.D2, LED1.anode, LED2.anode
  N3: lel.5V, J1.pin2
  N4: lel.GND, R1.Pin_0, R2.Pin_0, R3.Pin_0
  N5: LED1.cathode, R2.Pin_1
  N6: LED2.cathode, R3.Pin_1
